// Logisim project N0.circ as structural Verilog: 1 circuit, main circuit main
module main (
  input  S0,
  input  go,
  input  S6,
  input  S8,
  input  S2,
  input  e2,
  input  k2,
  input  k1,
  input  b1,
  input  e1,
  output out_11
);

  wire and_1_out, and_2_out, and_3_out, and_4_out, xor_1_out, xor_2_out;

  and and_1 (and_1_out, S0, go);
  xor xor_1 (xor_1_out, e2, k2);
  xor xor_2 (xor_2_out, b1, e1);
  and and_2 (and_2_out, S6, k2, ~e2);  // AND_Gate
  and and_3 (and_3_out, S2, xor_1_out);
  and and_4 (and_4_out, S8, ~k1, xor_2_out);  // AND_Gate
  or or_1 (out_11, and_1_out, and_2_out, and_3_out, and_4_out);
endmodule
