// Logisim project N1.circ as structural Verilog: 1 circuit, main circuit main
module main (
  input  S1,
  input  S2,
  input  S4,
  input  S5,
  input  S6,
  input  S8,
  input  S11,
  input  k1,
  input  b1,
  input  k2,
  input  e2,
  input  e1,
  output N1
);

  wire and_1_out, and_2_out, and_3_out, xor_1_out;

  and and_1 (and_1_out, S2, k2, ~e2);  // AND_Gate
  and and_2 (and_2_out, S6, k2, ~e2);  // AND_Gate
  xor xor_1 (xor_1_out, k1, e1);
  and and_3 (and_3_out, S8, xor_1_out, ~b1);  // AND_Gate
  or or_1 (N1, S1, and_1_out, S4, S5, and_2_out, S11, and_3_out);
endmodule
