// Logisim project N2.circ as structural Verilog: 1 circuit, main circuit main
module main (
  input  S2,
  input  S3,
  input  S5,
  input  S6,
  input  S11,
  input  k2,
  input  e2,
  output N2
);

  wire and_1_out, and_2_out;

  and and_1 (and_1_out, S2, ~k2, e2);  // AND_Gate
  and and_2 (and_2_out, S6, ~e2, k2);  // AND_Gate
  or or_1 (N2, S3, and_1_out, S5, and_2_out, S11);
endmodule
