// Logisim project N3.circ as structural Verilog: 1 circuit, main circuit main
module main (
  input  S7,
  input  S8,
  input  S9,
  input  S10,
  input  k1,
  input  b1,
  input  e1,
  output N3
);

  wire and_1_out, and_2_out, xor_1_out;

  xor xor_1 (xor_1_out, k1, b1);
  and and_1 (and_1_out, S8, ~e1, xor_1_out);  // AND_Gate
  and and_2 (and_2_out, S8, ~k1, ~b1, e1);  // AND_Gate
  or or_1 (N3, S7, and_2_out, S9, S10, and_1_out);
endmodule
