// Logisim project SpecialClock.circ as structural Verilog: 1 circuit, main circuit main
module main (
  input  go,
  input  button,
  input  i__n,
  input  ClockIn,
  output ClockOut
);

  wire and_1_out, and_2_out, and_3_out, and_4_out, comparator_1_lt, comparator_2_lt, counter_2_q, counter_4_q;
  wire [1:0] comparator_3_eq;
  wire [3:0] counter_1_q, counter_3_q;
  wire [7:0] counter_5_q;

  Button button_1 ();  // open: out
  Clock clock_1 ();  // open: out
  Button button_2 ();  // open: out
  Counter #(.width(4), .max('hf)) counter_1 (
    .Q(counter_1_q), .clk(and_1_out), .clr(and_3_out));  // open: load, D, count, carry
  and and_1 (and_1_out, ClockIn, comparator_1_lt);
  and and_2 (and_2_out, ClockIn, comparator_2_lt);
  and and_3 (and_3_out, go, counter_2_q);
  Counter #(.width(1), .max('h1), .trigger("falling")) counter_2 (
    .Q(counter_2_q), .clk(comparator_1_lt), .clr(go));  // open: load, D, count, carry
  Counter #(.width(4), .max('hf)) counter_3 (
    .Q(counter_3_q), .clk(and_2_out), .clr(and_4_out));  // open: load, D, count, carry
  and and_4 (and_4_out, button, counter_4_q);
  Counter #(.width(1), .max('h1), .trigger("falling")) counter_4 (
    .Q(counter_4_q), .clk(comparator_2_lt), .clr(button));  // open: load, D, count, carry
  Comparator #(.width(4)) comparator_1 (.a(counter_1_q), .b(4'b0010), .lt(comparator_1_lt));  // open: gt, eq
  Comparator #(.width(4)) comparator_2 (.a(counter_3_q), .b(4'b0011), .lt(comparator_2_lt));  // open: gt, eq
  Counter #(.trigger("falling")) counter_5 (
    .Q(counter_5_q), .clk(comparator_1_lt));  // open: load, D, count, carry, clr
  Comparator comparator_3 (.a(counter_5_q), .b(8'h2), .eq(comparator_3_eq[0]));  // open: gt, lt
  Counter #(.width(1), .max('h1)) counter_6 (
    .Q(comparator_3_eq[1]), .clk(i__n), .clr(go));  // open: load, D, count, carry
  Multiplexer #(.select(2), .enable("false")) multiplexer_1 (
    .in0(and_1_out), .in1(and_2_out), .in2(ClockIn), .in3(ClockIn), .out(ClockOut), .sel(comparator_3_eq));
  Counter counter_7 ();  // open: load, D, count, Q, carry, clk, clr
endmodule
