// Logisim project control_unit_v1.circ as structural Verilog: 1 circuit, main circuit main
module main (
  input  go,
  input  clk,
  input  k1,
  input  e1,
  input  b1,
  input  k2,
  input  e2,
  output N0,
  output N1,
  output N2,
  output N3,
  output en_i,
  output ld,
  output en_k,
  output m4_0,
  output en_res,
  output en_out,
  output m2,
  output m11,
  output m10,
  output m3,
  output m5,
  output m41,
  output m6,
  output m7,
  output en_ram
);

  wire main_1_s0, main_1_s1, main_1_s2, main_1_s5, main_1_s8, main_2_out_11, main_3_n1, main_4_n2, main_5_n3;

  D_Flip_Flop D0 (.clk(clk), .D(main_2_out_11), .Q(N0));  // open: Qn, preset, en, reset
  D_Flip_Flop D1 (.clk(clk), .D(main_3_n1), .Q(N1));  // open: Qn, preset, en, reset
  D_Flip_Flop D2 (.clk(clk), .D(main_4_n2), .Q(N2));  // open: Qn, preset, en, reset
  D_Flip_Flop D3 (.clk(clk), .D(main_5_n3), .Q(N3));  // open: Qn, preset, en, reset
  variable_path_main main_1 (
    .P3(N3), .P2(N2), .P1(N1), .P0(N0), .S0(main_1_s0), .S1(main_1_s1), .S2(main_1_s2), .S3(m10), .S4(m2),
    .S5(main_1_s5), .S6(m6), .S7(m4_0), .S8(main_1_s8), .S9(m5), .S10(m41), .S11(m3));
  or or_1 (en_ram, main_1_s5, m10, m4_0);
  N0_main main_2 (
    .S0(main_1_s0), .go(go), .S6(m6), .S8(main_1_s8), .S2(main_1_s2), .e2(e2), .k2(k2), .k1(k1), .b1(b1),
    .e1(e1), .out_11(main_2_out_11));
  N1_main main_3 (
    .S1(main_1_s1), .S2(main_1_s2), .S4(m2), .S5(main_1_s5), .S6(m6), .S8(main_1_s8), .S11(m3), .k1(k1),
    .b1(b1), .k2(k2), .e2(e2), .N1(main_3_n1), .e1(e1));
  N2_main main_4 (.S2(main_1_s2), .S3(m10), .S5(main_1_s5), .S6(m6), .S11(m3), .k2(k2), .e2(e2), .N2(main_4_n2));
  N3_main main_5 (.S7(m4_0), .S8(main_1_s8), .S9(m5), .S10(m41), .k1(k1), .b1(b1), .e1(e1), .N3(main_5_n3));
  or or_2 (en_i, main_1_s1, m2);
  or or_3 (ld, main_1_s5, m4_0);
  or or_4 (en_k, main_1_s1, m3);
  or or_5 (en_res, main_1_s5, m5);
  or or_6 (en_out, main_1_s1, m4_0, m41);

  assign m7 = m5;
  assign m11 = m4_0;
endmodule
