// Logisim project datapath.circ as structural Verilog: 1 circuit, main circuit main
// m2
module main (
  input  [15:0] number,
  input  clk,
  input  en_ram,
  input  [7:0] number_amount,
  input  m2,
  input  en_i,
  input  [1:0] m1,
  input  ld,
  input  m3,
  input  en_k,
  input  m5,
  input  [1:0] m4,
  input  en_res,
  input  en_out,
  input  m6,
  input  m7,
  output b1,
  output e1,
  output k1,
  output [15:0] result,
  output e2,
  output k2
);

  wire [7:0] adder_1_out, adder_2_out, i_q, k_q, multiplexer_1_out, multiplexer_2_out, multiplexer_3_out,
       multiplexer_6_out;
  wire [15:0] multiplexer_4_out, multiplexer_5_out, multiplexer_7_out, out_q, ram_1_data, subtractor_1_out,
       subtractor_2_out;

  Register i (.D(multiplexer_1_out), .en(en_i), .Q(i_q), .clk(clk));  // open: clr
  Multiplexer #(.width(8), .enable("false")) multiplexer_1 (
    .in0({8{1'b0}}), .in1(adder_1_out), .out(multiplexer_1_out), .sel(m2));
  Multiplexer #(.select(2), .width(8), .enable("false")) multiplexer_2 (
    .in0({8{1'b0}}), .in1(i_q), .in2(k_q), .out(multiplexer_2_out), .sel(m1));  // open: in3
  Adder adder_1 (.a(i_q), .b(8'h1), .out(adder_1_out));  // open: cin, cout
  Multiplexer #(.width(8), .enable("false")) multiplexer_3 (
    .in0(8'h1), .in1(adder_2_out), .out(multiplexer_3_out), .sel(m3));
  Register k (.D(multiplexer_3_out), .en(en_k), .Q(k_q), .clk(clk));  // open: clr
  RAM #(.dataWidth(16), .bus("separate")) ram_1 (
    .addr(multiplexer_2_out), .din(number), .data(ram_1_data), .sel(en_ram), .clk(clk), .ld(ld));  // open: str, clr
  Multiplexer #(.width(16), .enable("false")) multiplexer_4 (
    .in0(ram_1_data), .in1(multiplexer_7_out), .out(multiplexer_4_out), .sel(m5));
  Adder adder_2 (.a(k_q), .b(8'h1), .out(adder_2_out));  // open: cin, cout
  Multiplexer #(.select(2), .width(16), .enable("false")) multiplexer_5 (
    .in0({16{1'b0}}), .in1(ram_1_data), .in2(multiplexer_7_out), .out(multiplexer_5_out), .sel(m4));  // open: in3
  Register #(.width(16)) out (.D(multiplexer_5_out), .en(en_out), .Q(out_q), .clk(clk));  // open: clr
  Register #(.width(16)) res (.D(multiplexer_4_out), .en(en_res), .Q(result), .clk(clk));  // open: clr
  Multiplexer #(.width(8), .enable("false")) multiplexer_6 (.in0(i_q), .in1(k_q), .out(multiplexer_6_out), .sel(m6));
  Subtractor #(.width(16)) subtractor_1 (.a(out_q), .b(result), .out(subtractor_1_out));  // open: bin, bout
  Subtractor #(.width(16)) subtractor_2 (.a(result), .b(out_q), .out(subtractor_2_out));  // open: bin, bout
  Comparator #(.width(16)) comparator_1 (.a(result), .b(out_q), .gt(b1), .eq(e1), .lt(k1));
  Comparator comparator_2 (.a(multiplexer_6_out), .b(number_amount), .eq(e2), .lt(k2));  // open: gt
  Multiplexer #(.width(16), .enable("false")) multiplexer_7 (
    .in0(subtractor_1_out), .in1(subtractor_2_out), .out(multiplexer_7_out), .sel(m7));
endmodule
