// Logisim project gcd.circ as structural Verilog: 1 circuit, main circuit main
module main (
  input  [7:0] of_NUMBERS,
  input  [15:0] NUMBER,
  output [15:0] RESULT,
  output N3,
  output N2,
  output N1,
  output N0
);

  wire and_1_out, clock_1_out, control_unit_en_i, control_unit_en_k, control_unit_en_out,
       control_unit_en_ram, control_unit_en_res, control_unit_ld, control_unit_m2, control_unit_m3,
       control_unit_m5, control_unit_m6, control_unit_m7, datapath_b1, datapath_e1, datapath_e2, datapath_k1,
       datapath_k2, Go_out, Input_out, main_1_clockout;
  wire [1:0] control_unit_m4_0, control_unit_m10;

  Button Go (.out(Go_out));
  Button Input (.out(Input_out));
  Clock clock_1 (.out(clock_1_out));
  control_unit_v1_main control_unit (
    .go(Go_out), .k1(datapath_k1), .e1(datapath_e1), .b1(datapath_b1), .k2(datapath_k2), .e2(datapath_e2),
    .en_ram(control_unit_en_ram), .m2(control_unit_m2), .clk(main_1_clockout), .m11(control_unit_m10[1]),
    .m10(control_unit_m10[0]), .m3(control_unit_m3), .m5(control_unit_m5), .m41(control_unit_m4_0[1]),
    .m6(control_unit_m6), .m7(control_unit_m7), .N0(N0), .N1(N1), .N2(N2), .N3(N3), .en_i(control_unit_en_i),
    .ld(control_unit_ld), .en_k(control_unit_en_k), .m4_0(control_unit_m4_0[0]),
    .en_res(control_unit_en_res), .en_out(control_unit_en_out));
  SpecialClock_main main_1 (
    .go(Go_out), .button(Input_out), .i__n(and_1_out), .ClockIn(clock_1_out), .ClockOut(main_1_clockout));
  and and_1 (and_1_out, N0, ~N1, N2, ~N3);  // AND_Gate
  datapath_main datapath (
    .number(NUMBER), .clk(main_1_clockout), .number_amount(of_NUMBERS), .m2(control_unit_m2),
    .en_i(control_unit_en_i), .m1(control_unit_m10), .ld(control_unit_ld), .m3(control_unit_m3),
    .en_k(control_unit_en_k), .m5(control_unit_m5), .m4(control_unit_m4_0), .en_res(control_unit_en_res),
    .en_out(control_unit_en_out), .m6(control_unit_m6), .m7(control_unit_m7), .k2(datapath_k2),
    .k1(datapath_k1), .e2(datapath_e2), .e1(datapath_e1), .b1(datapath_b1), .en_ram(control_unit_en_ram),
    .result(RESULT));
endmodule
