// Logisim project variable_path.circ as structural Verilog: 1 circuit, main circuit main
module main (
  input  P3,
  input  P2,
  input  P1,
  input  P0,
  output S0,
  output S1,
  output S2,
  output S3,
  output S4,
  output S5,
  output S6,
  output S7,
  output S8,
  output S9,
  output S10,
  output S11
);

  Decoder #(.select(4), .enable("false")) decoder_1 (
    .out0(S0), .out1(S1), .out2(S2), .out3(S3), .out4(S4), .out5(S5), .out6(S6), .out7(S7), .out8(S8),
    .out9(S9), .out10(S10), .out11(S11), .sel({P3, P2, P1, P0}));  // open: out12, out13, out14, out15
endmodule
